# Fritzing sketch alcohol detection diagram (saved by Fritzing 0.9.6b)
breadboards: 1

parts:
  Part1 = Arduino Nano (Rev3.0)
  R1 = Resistor [tolerance=±5% resistance=220 power=0.25 package=THT]
  R2 = Resistor [tolerance=±5% resistance=220 power=0.25 package=THT]
  R3 = Resistor [tolerance=±5% resistance=220 power=0.25 package=THT]
  LED2 = RGB LED (com. cathode, rbg) [package="5 mm [THT]"]
  BAT1 = BC9VPC [package=bc9vpc]
  Mod1 = MQ-7 breakout
  LCD2004-I2C1 = LCD2004-I2C

nets:
  GND: Part1.GND, LED2.common_cathode, BAT1.V-, Mod1.GND, LCD2004-I2C1.GND
  N1: Part1.D5, R1.Pin_0
  N2: Part1.D6, R2.Pin_0
  N3: Part1.D7, R3.Pin_0
  VIN: Part1.VIN, BAT1.V+, LCD2004-I2C1.VCC
  5V: Part1.5V, Mod1.VCC
  N4: Part1.A5, LCD2004-I2C1.SCL
  N5: Part1.A4, LCD2004-I2C1.SDA
  N6: Part1.A3, Mod1.AO
  N7: R1.Pin_1, LED2.red_anode
  N8: R2.Pin_1, LED2.blue_anode
  N9: R3.Pin_1, LED2.green_anode

custom parts:
  MQ-7 breakout: MQ-5 gas sensor
  LCD2004-I2C: A standard character display with 4x20 characters. Comes in many colors with LCM2004 IIC attached.
